# Fritzing sketch LED Reverse (saved by Fritzing 0.8.7b)
breadboards: 1

parts:
  Part1 = Arduino Uno (Rev3)
  LED1 = LED - 5mm [color="Red (633nm)" package="5 mm [THT]"]
  R1 = Resistor [tolerance=±5% resistance=220 package=THT]

nets:
  N1: Part1.D13/SCK, LED1.cathode
  N2: Part1.5V, R1.Pin_0
  N3: LED1.anode, R1.Pin_1
