# Fritzing sketch LCD_Project_2 (saved by Fritzing 0.8.7b)
breadboards: 1

parts:
  Part1 = Arduino Uno (Rev3)
  S1 = Momentary Switch [package=ksa_sealed_tac_switch]
  S2 = Momentary Switch [package=ksa_sealed_tac_switch]
  LCD1 = LCD screen
  LED1 = LED - 5mm [color="Red (633nm)" package="5 mm [THT]"]
  R1 = Rotary Potentiometer (Small) [maximum_resistance=100kΩ package=THT]
  R2 = Rotary Potentiometer (Small) [maximum_resistance=100kΩ package=THT]
  DS1 = DS18B20 1-Wire Temperature Sensor [part_number=DS18B20]  # not connected
  R3 = Resistor [tolerance=±5% resistance=100 package=THT]

nets:
  N1: Part1.D8, S1.1, S1.2
  N2: Part1.D9_PWM, S2.3, S2.4
  N3: Part1.D11_PWM/MOSI, LCD1.E
  N4: Part1.D12/MISO, LCD1.RS
  N5: Part1.D2, LCD1.DB7
  N6: Part1.D3_PWM, LCD1.DB6
  N7: Part1.D4, LCD1.DB5
  N8: Part1.D5_PWM, LCD1.DB4
  N9: Part1.D6_PWM, LED1.anode
  5V: Part1.5V, LCD1.VDD, LCD1.LED+, R1.leg2, R2.leg1
  GND: Part1.GND, S1.3, S1.4, S2.1, S2.2, LCD1.VSS, LCD1.R/W, R1.leg1, R2.leg2, R3.Pin_0
  N10: LCD1.V0, R2.wiper
  N11: LCD1.LED-, R1.wiper
  N12: LED1.cathode, R3.Pin_1
