# Fritzing sketch LED ScannerWithSwitchAndSpeaker (saved by Fritzing 0.8.7b)
breadboards: 1

parts:
  Part1 = Arduino Uno (Rev3)
  LED1 = LED - 5mm [color="Red (633nm)" package="5 mm [THT]"]
  LED2 = LED - 5mm [color="Red (633nm)" package="5 mm [THT]"]
  LED3 = LED - 5mm [color="Red (633nm)" package="5 mm [THT]"]
  LED4 = LED - 5mm [color="Red (633nm)" package="5 mm [THT]"]
  LED5 = LED - 5mm [color="Red (633nm)" package="5 mm [THT]"]
  LED6 = LED - 5mm [color="Red (633nm)" package="5 mm [THT]"]
  LED7 = LED - 5mm [color="Red (633nm)" package="5 mm [THT]"]
  R1 = Resistor [tolerance=±5% resistance=220 package=THT]
  R2 = Resistor [tolerance=±5% resistance=220 package=THT]
  R3 = Resistor [tolerance=±5% resistance=220 package=THT]
  R4 = Resistor [tolerance=±5% resistance=220 package=THT]
  R5 = Resistor [tolerance=±5% resistance=220 package=THT]
  R6 = Resistor [tolerance=±5% resistance=220 package=THT]
  R7 = Resistor [tolerance=±5% resistance=220 package=THT]
  S1 = Pushbutton [package="[THT]"]
  MIC1 = Microphone
  C1 = Ceramic Capacitor [capacitance=100nF package="200 mil [THT, multilayer]"]

nets:
  N1: Part1.D8, LED6.anode
  N2: Part1.D9_PWM, LED5.anode
  N3: Part1.D10_PWM/SS, LED4.anode
  N4: Part1.D11_PWM/MOSI, LED3.anode
  N5: Part1.D12/MISO, LED2.anode
  N6: Part1.D13/SCK, LED1.anode
  N7: Part1.GND, R1.Pin_1, R2.Pin_1, R3.Pin_1, R4.Pin_1, R5.Pin_1, R6.Pin_1, R7.Pin_1, S1.Pin_1, S1.Pin_2, C1.1
  N8: Part1.D5_PWM, MIC1.pin1
  N9: Part1.D6_PWM, S1.Pin_3, S1.Pin_4
  N10: Part1.D7, LED7.anode
  N11: LED1.cathode, R1.Pin_0
  N12: LED2.cathode, R2.Pin_0
  N13: LED3.cathode, R3.Pin_0
  N14: LED4.cathode, R4.Pin_0
  N15: LED5.cathode, R5.Pin_0
  N16: LED6.cathode, R6.Pin_0
  N17: LED7.cathode, R7.Pin_0
  N18: MIC1.pin2, C1.0
