# Fritzing sketch SevenSegment2 (saved by Fritzing 0.8.7b)
breadboards: 1

parts:
  Part1 = Arduino Uno (Rev3)
  R1 = Resistor [tolerance=±5% resistance=220 package=THT]
  R2 = Resistor [tolerance=±5% resistance=220 package=THT]
  R3 = Resistor [tolerance=±5% resistance=220 package=THT]
  R4 = Resistor [tolerance=±5% resistance=220 package=THT]
  R5 = Resistor [tolerance=±5% resistance=220 package=THT]
  R6 = Resistor [tolerance=±5% resistance=220 package=THT]
  R7 = Resistor [tolerance=±5% resistance=220 package=THT]
  R8 = Resistor [tolerance=±5% resistance=220 package=THT]

nets:
  N1: Part1.D8, R8.Pin_1
  N2: Part1.D9_PWM, R4.Pin_0
  N3: Part1.D2, R1.Pin_0
  N4: Part1.D3_PWM, R3.Pin_1
  N5: Part1.D4, R7.Pin_1
  N6: Part1.D5_PWM, R6.Pin_0
  N7: Part1.D6_PWM, R5.Pin_0
  N8: Part1.D7, R2.Pin_0

notes:
  LED display fits here. Pins go in columns 5-10
