# Fritzing sketch SevenSegment4 (saved by Fritzing 0.8.7b)
breadboards: 1

parts:
  Part1 = Arduino Uno (Rev3)
  R1 = Resistor [tolerance=±5% resistance=220 package=THT]
  R2 = Resistor [tolerance=±5% resistance=220 package=THT]
  R3 = Resistor [tolerance=±5% resistance=220 package=THT]
  R4 = Resistor [tolerance=±5% resistance=220 package=THT]
  R5 = Resistor [tolerance=±5% resistance=220 package=THT]
  R6 = Resistor [tolerance=±5% resistance=220 package=THT]
  R7 = Resistor [tolerance=±5% resistance=220 package=THT]
  R8 = Resistor [tolerance=±5% resistance=220 package=THT]
  Q1 = NPN-Transistor [package="TO92 [THT]"]
  Q2 = NPN-Transistor [package="TO92 [THT]"]
  Q3 = NPN-Transistor [package="TO92 [THT]"]
  Q4 = NPN-Transistor [package="TO92 [THT]"]
  R9 = Resistor [tolerance=±5% resistance=1k package=THT]
  R10 = Resistor [tolerance=±5% resistance=1k package=THT]
  R11 = Resistor [tolerance=±5% resistance=1k package=THT]
  R12 = Resistor [tolerance=±5% resistance=1k package=THT]

nets:
  N1: Part1.D8, R8.Pin_1
  N2: Part1.D9_PWM, R4.Pin_0
  N3: Part1.D10_PWM/SS, R9.Pin_0
  N4: Part1.D11_PWM/MOSI, R10.Pin_0
  N5: Part1.D12/MISO, R11.Pin_0
  N6: Part1.D13/SCK, R12.Pin_0
  N7: Part1.GND, Q1.E, Q2.E, Q3.E, Q4.E
  N8: Part1.D2, R1.Pin_0
  N9: Part1.D3_PWM, R3.Pin_1
  N10: Part1.D4, R7.Pin_1
  N11: Part1.D5_PWM, R6.Pin_0
  N12: Part1.D6_PWM, R5.Pin_0
  N13: Part1.D7, R2.Pin_0
  N14: Q1.B, R12.Pin_1
  N15: Q2.B, R11.Pin_1
  N16: Q3.B, R10.Pin_1
  N17: Q4.B, R9.Pin_1

notes:
  LED Display
