# Fritzing sketch ShiftRegister (saved by Fritzing 0.8.7b)
breadboards: 1

parts:
  Part1 = Arduino Uno (Rev3)
  IC1 = IC, DIP package, 16 pins [chip_label=74HC595]
  R1 = Resistor [tolerance=±5% resistance=220 package=THT]
  R2 = Resistor [tolerance=±5% resistance=220 package=THT]
  R3 = Resistor [tolerance=±5% resistance=220 package=THT]
  R4 = Resistor [tolerance=±5% resistance=220 package=THT]
  R5 = Resistor [tolerance=±5% resistance=220 package=THT]
  R6 = Resistor [tolerance=±5% resistance=220 package=THT]
  R7 = Resistor [tolerance=±5% resistance=220 package=THT]
  R8 = Resistor [tolerance=±5% resistance=220 package=THT]
  LED1 = LED - 5mm [color="Red (633nm)" package="5 mm [THT]"]
  LED2 = LED - 5mm [color="Red (633nm)" package="5 mm [THT]"]
  LED3 = LED - 5mm [color="Red (633nm)" package="5 mm [THT]"]
  LED4 = LED - 5mm [color="Red (633nm)" package="5 mm [THT]"]
  LED5 = LED - 5mm [color="Red (633nm)" package="5 mm [THT]"]
  LED6 = LED - 5mm [color="Red (633nm)" package="5 mm [THT]"]
  LED7 = LED - 5mm [color="Red (633nm)" package="5 mm [THT]"]
  LED8 = LED - 5mm [color="Red (633nm)" package="5 mm [THT]"]

nets:
  N1: Part1.D10_PWM/SS, IC1.pin14
  N2: Part1.D11_PWM/MOSI, IC1.pin12
  N3: Part1.D12/MISO, IC1.pin11
  N4: Part1.5V, IC1.pin10, IC1.pin16
  N5: Part1.GND, IC1.pin8, IC1.pin13, LED1.cathode, LED2.cathode, LED3.cathode, LED4.cathode, LED5.cathode, LED7.cathode, LED8.cathode
  N6: IC1.pin1, R2.Pin_1
  N7: IC1.pin2, R3.Pin_1
  N8: IC1.pin3, R4.Pin_1
  N9: IC1.pin4, R5.Pin_1
  N10: IC1.pin5, R6.Pin_0
  N11: IC1.pin6, R7.Pin_0
  N12: IC1.pin15, R1.Pin_1
  N13: R1.Pin_0, LED4.anode
  N14: R2.Pin_0, LED5.anode
  N15: R3.Pin_0, LED6.anode
  N16: R4.Pin_0, LED7.anode
  N17: R5.Pin_0, LED8.anode
  N18: R6.Pin_1, LED1.anode
  N19: R7.Pin_1, LED2.anode
  N20: R8.Pin_1, LED3.anode
